# Fritzing sketch schematics (saved by Fritzing 0.9.3b)
breadboards: 1

parts:
  Part1 = Arduino Nano (Rev3.0)
  U1 = RFID RC522 SIP - 8 pins [chip_label="RFID RC522" package="SIP (Single Inline) [THT]"]
  LED1 = LED - 3mm [color="Red (633nm)" package="3 mm [THT]"]
  LED2 = LED - 3mm [color="Blue (470nm)" package="3 mm [THT]"]
  R1 = Resistor [tolerance=±5% resistance=220 package="0805 [SMD]"]
  R2 = Resistor [tolerance=±5% resistance=220 package="0805 [SMD]"]

nets:
  GND: Part1.GND, U1.GND, R1.Pin_1, R2.Pin_1
  N1: Part1.D7, LED2.anode
  N2: Part1.D8, LED1.anode
  N3: Part1.D9, U1.RST
  N4: Part1.D10, U1.NSS
  N5: Part1.D11/MOSI, U1.MOSI
  N6: Part1.D12/MISO, U1.MISO
  3V3: Part1.3V3, U1.VCC
  N7: Part1.D13/SCK, U1.SCK
  N8: LED1.cathode, R1.Pin_0
  N9: LED2.cathode, R2.Pin_0

custom parts:
  RFID RC522 SIP - 8 pins: A SIP stand-in part for RFID RC522 . With 8 pins on a 300 mil single inline package (SIP) footprint.
